# Fritzing sketch ESP32 and MAG3110 (saved by Fritzing 0.9.3b)

parts:
  Part5 = MAG3110
  U1 = lolin

nets:
  N1: Part5.GND, U1.connector37
  N2: Part5.VCC, U1.connector34
  N3: Part5.SDA, U1.connector32
  N4: Part5.SCL, U1.connector33

custom parts:
  MAG3110: Sparkfun MAG3110 Breakout
