# Fritzing sketch LOLIN32 and GA1A12S202 (saved by Fritzing 0.9.3b)

parts:
  Part1 = Adafruit GA1A1S202WP [part_number="Adafruit #1384"]
  U1 = lolin

nets:
  N1: Part1.VCC, U1.connector0
  N2: Part1.OUT, U1.connector2
  N3: Part1.GND, U1.connector15

custom parts:
  Adafruit GA1A1S202WP: Upgrade a project that uses a photocell with the GA1A12S202 analog light sensor. Like a CdS photo-cell, the sensor does not require a microcontroller, the analog voltage output increases with the amount of light shining on the sensor face. This sensor has a lot of improvements that make it better for nearly any project. The biggest improvement over plain photocells is a true log-lin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
