# Fritzing sketch LOLIN32 and TSL2561 (saved by Fritzing 0.9.3b)

parts:
  U1 = lolin
  Part2 = Adafruit TSL2561 [part_number="Adafruit #439"]

nets:
  N1: U1.connector32, Part2.SDA
  N2: U1.connector33, Part2.SCL
  N3: U1.connector34, Part2.3.3V
  N4: U1.connector37, Part2.GND

custom parts:
  Adafruit TSL2561: The TSL2561 luminosity sensor is an advanced digital light sensor, ideal for use in a wide range of light situations. Compared to low cost CdS cells, this sensor is more precise, allowing for exact lux calculations and can be configured for different gain/timing ranges to detect light ranges from up to 0.1 - 40,000+ Lux on the fly. The best part of this sensor is that it contains both infrared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
