# Fritzing sketch esp32 and ADXL335 (saved by Fritzing 0.9.3b)

parts:
  U1 = lolin
  Part1 = Adafruit ADXL335 [part_number="Adafruit #163"]

nets:
  N1: U1.connector0, Part1.VIN
  N2: U1.connector2, Part1.XOUT
  N3: U1.connector3, Part1.YOUT
  N4: U1.connector4, Part1.ZOUT
  N5: U1.connector15, Part1.GND

custom parts:
  Adafruit ADXL335: We've updated our favorite triple-axis accelerometer to now have an on-board 3.3V regulator - making it a perfect choice for interfacing with a 5V microcontroller such as the Arduino. This breakout comes with 3 analog outputs for X, Y and Z axis measurements on a 0.75"x0.75" breakout board. The ADXL335 is the latest and greatest from Analog Devices, known for their exceptional quality MEMS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
