# Fritzing sketch esp32 and MPL3115A2 (saved by Fritzing 0.9.3b)

parts:
  U1 = lolin
  Part1 = MPL3115A2 I2C Barometric Pressure, Altitude, Temperature Sensor

nets:
  N1: U1.connector0, Part1.VIN
  N2: U1.connector32, Part1.SDA
  N3: U1.connector33, Part1.SCL
  N4: U1.connector37, Part1.GND

custom parts:
  MPL3115A2 I2C Barometric Pressure, Altitude, Temperature Sensor: This pressure sensor from Freescale is a great low-cost sensing solution for precision measurement of barometric pressure and altitude. The MPL3115A2 has a typical 1.5 Pascal resolution, which can resolve altitude at 0.3 meters (compare to the BMP180 which can do 0.17m). It has some upsides compared to the BMP180, such as interrupt outputs for ultra-low power usage, and its also a heck of a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
