# Fritzing sketch esp32 and VEML6070 (saved by Fritzing 0.9.3b)

parts:
  U1 = lolin
  Part2 = VEML6070 [part_number=VEML6070]

nets:
  N1: U1.connector0, Part2.VDD
  N2: U1.connector32, Part2.SDA
  N3: U1.connector33, Part2.SCL
  N4: U1.connector37, Part2.GND

custom parts:
  VEML6070: This little sensor is a great way to add UV light sensing to any microcontroller project. The VEML6070 from Vishay has a true UV A light sensor and an I2C-controlled ADC that will take readings and integrate them for you over ~60ms to 500ms.
