# Fritzing sketch esp32 and VL53L0X (saved by Fritzing 0.9.3b)

parts:
  U1 = lolin
  Part1 = Adafruit VL53L0X Time of Flight Distance Sensor [part_number="Adafruit #3317"]

nets:
  N1: U1.connector0, Part1.VIN
  N2: U1.connector32, Part1.SDA
  N3: U1.connector33, Part1.SCL
  N4: U1.connector37, Part1.GND

custom parts:
  Adafruit VL53L0X Time of Flight Distance Sensor: The VL53L0X is a Time of Flight distance sensor like no other you've used! The sensor contains a very tiny invisible laser source, and a matching sensor. The VL53L0X can detect the "time of flight", or how long the light has taken to bounce back to the sensor. Since it uses a very narrow light source, it is good for determining distance of only the surface directly in front of it. Unlike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
