# Fritzing sketch esp32 and bme280 (saved by Fritzing 0.9.3b)

parts:
  U1 = lolin
  Part2 = BME280 Breakout

nets:
  N1: U1.connector32, Part2.SDI/SDA
  N2: U1.connector33, Part2.SCK/SCL
  N3: U1.connector34, Part2.3.3V
  N4: U1.connector37, Part2.GND
