# Fritzing sketch esp32 and bmp280 (saved by Fritzing 0.9.3b)

parts:
  Part1 = Adafruit_BMP280
  U1 = lolin

nets:
  N1: Part1.3.3V, U1.connector34
  N2: Part1.GND, U1.connector37
  N3: Part1.SCK/SCL, U1.connector33
  N4: Part1.SDI/SDA, U1.connector32

custom parts:
  Adafruit_BMP280: Bosch has stepped up their game with their new BMP280 sensor, an environmental sensor with temperature, barometric pressure that is the next generation upgrade to the BMP085/BMP180/BMP183. This sensor is great for all sorts of weather sensing and can even be used in both I2C and SPI! This precision sensor from Bosch is the best low-cost, precision sensing solution for measuring barometric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
