# Fritzing sketch esp32 and dht12 (saved by Fritzing 0.9.3b)

parts:
  DHT1 = DHT12 Humitidy and Temperature Sensor I2C.
  U1 = lolin

nets:
  N1: DHT1.VDD, U1.connector34
  N2: DHT1.SDA, U1.connector32
  N3: DHT1.GND, U1.connector20
  N4: DHT1.SCL, U1.connector33

custom parts:
  DHT12 Humitidy and Temperature Sensor I2C.: DHT12 Humidity and Temperature Sensor I2C. Supply voltage: 2.7V to 5.5V Current: Standby 30uA, Active 800uA Temperature: -20ºC to 60ºC, res. 0.1ºC Humidity: 20%RH to 95%RH, res. 0.1%RH ID I2C 0x5c
