# Fritzing sketch esp32 and lm35 (saved by Fritzing 0.9.3b)

parts:
  U1 = lolin
  T1 = LM35 Temperature Sensor [package="TO92 [THT]"]

nets:
  N1: U1.connector0, T1.+Vs
  N2: U1.connector2, T1.Vout
  N3: U1.connector15, T1.GND
