# Fritzing sketch esp32 and temt6000 (saved by Fritzing 0.9.3b)

parts:
  Part1 = Ambient Light Sensor (TEMT6000 Breakout Board)
  U1 = lolin

nets:
  N1: Part1.VCC, U1.connector0
  N2: Part1.GND, U1.connector15
  N3: Part1.S, U1.connector2
