# Fritzing sketch esp32 and ws2812 (saved by Fritzing 0.9.3b)

parts:
  U1 = lolin
  Part3 = ws2812b [package="smd 2812b"]

nets:
  N1: U1.connector18, Part3.DIN
  N2: U1.connector20, Part3.VSS
  N3: U1.connector34, Part3.VDD
