# Fritzing sketch lolin32 and L3GD20 (saved by Fritzing 0.9.3b)

parts:
  U1 = lolin
  Part2 = L3GD20H Triple-Axis Gyro Breakout Board [part_number=1032]

nets:
  N1: U1.connector25, Part2.+3V3
  N2: U1.connector30, Part2.GND
  N3: U1.connector32, Part2.SDA/SDI/SDO
  N4: U1.connector33, Part2.SCL/SPC

custom parts:
  L3GD20H Triple-Axis Gyro Breakout Board: This breakout board is based around the latest gyro technology, the L3GD20H from STMicro. It's the upgrade to the L3G4200 with three full axes of sensing. The chip can be set to ±250, ±500, or ±2000 degree-per-second scale for a large range of sensitivity. The chip supports both I2C and SPI so you can interface with any microcontroller easily. Includes level shifting circuitry so you can use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
