# Fritzing sketch lolin32 and TCS34725 (saved by Fritzing 0.9.3b)

parts:
  U1 = lolin
  Part1 = Adafruit TCS34725 RGB Color Sensor [part_number="Adafruit #1334"]

nets:
  N1: U1.connector30, Part1.GND
  N2: U1.connector32, Part1.SDA
  N3: U1.connector33, Part1.SCL
  N4: U1.connector34, Part1.+3V3

custom parts:
  Adafruit TCS34725 RGB Color Sensor: Your electronics can now see in dazzling color with this lovely color light sensor. We found the best color sensor on the market, the TCS34725, which has RGB and Clear light sensing elements. An IR blocking filter, integrated on-chip and localized to the color sensing photodiodes, minimizes the IR spectral component of the incoming light and allows color measurements to be made accurately. The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
