# Fritzing sketch lolin32 and adxl345 (saved by Fritzing 0.9.3b)

parts:
  U1 = lolin
  Part2 = Adafruit ADXL345 [part_number="Adafruit #1231"]

nets:
  N1: U1.connector32, Part2.SDA/SDIO
  N2: U1.connector33, Part2.SCL
  N3: U1.connector34, Part2.3.3V
  N4: U1.connector37, Part2.GND

custom parts:
  Adafruit ADXL345: Filling out our accelerometer offerings, we now have the really lovely digital ADXL345 from Analog Devices, a triple-axis accelerometer with digital I2C and SPI interface breakout. We added an on-board 3.3V regulator and logic-level shifting circuitry, making it a perfect choice for interfacing with any 3V or 5V microcontroller such as the Arduino. The sensor has three axes of measurements, X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
