# Fritzing sketch lolin32 and bmp180 (saved by Fritzing 0.9.3b)

parts:
  U1 = lolin
  Part3 = Adafruit BMP180

nets:
  N1: U1.connector32, Part3.SDA
  N2: U1.connector33, Part3.SCL
  N3: U1.connector34, Part3.+3V3
  N4: U1.connector37, Part3.GND

custom parts:
  Adafruit BMP180: This precision sensor from Bosch is the best low-cost sensing solution for measuring barometric pressure and temperature. Because pressure changes with altitude you can also use it as an altimeter! The sensor is soldered onto a PCB with a 3.3V regulator, I2C level shifter and pull-up resistors on the I2C pins. The BMP180 is the next-generation of sensors from Bosch, and replaces the BMP085.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
