# Fritzing sketch lolin32 and dht11 (saved by Fritzing 0.9.3b)

parts:
  Part1 = KY-015 Temperature & Humidity Sensor Module [package="Breakout board"]
  U1 = lolin

nets:
  N1: Part1.S, U1.connector18
  N2: Part1.Vin, U1.connector0
  N3: Part1.-, U1.connector15

custom parts:
  KY-015 Temperature & Humidity Sensor Module: KY-015 temperature and humidity sensor module, provides a low-latency serial interface to measure humidity and temperature.
