# Fritzing sketch lolin32 and dht22 (saved by Fritzing 0.9.3b)
breadboards: 1

parts:
  U1 = lolin
  DHT1 = DHT22 Humidity and Temperature Sensor
  R1 = Resistor [tolerance=±5% resistance=1k package=THT]

nets:
  N1: U1.connector0, DHT1.VDD, R1.Pin_1
  N2: U1.connector15, DHT1.GND
  N3: U1.connector18, DHT1.DATA, R1.Pin_0
