# Fritzing sketch lolin32 and hmc5883 (saved by Fritzing 0.9.3b)

parts:
  U1 = lolin
  Part1 = Triple Axis Magnetometer - HMC5883 Breakout

nets:
  N1: U1.connector31, Part1.GND
  N2: U1.connector32, Part1.SDA
  N3: U1.connector33, Part1.SCL
  N4: U1.connector34, Part1.VCC
