# Fritzing sketch lolin32 and lsm303 (saved by Fritzing 0.9.3b)

parts:
  U1 = lolin
  Part1 = Adafruit LSM303DLHC Triple-axis Accelerometer+Magnetometer (Compass) [part_number="Adafruit #1120"]

nets:
  N1: U1.connector25, Part1.3.3V
  N2: U1.connector30, Part1.GND
  N3: U1.connector32, Part1.SDA
  N4: U1.connector33, Part1.SCL

custom parts:
  Adafruit LSM303DLHC Triple-axis Accelerometer+Magnetometer (Compass): He told you "Go West, young maker!" - but you don't know which way is West! Ah, if only you had this triple-axis accelerometer/magnetometer compass module. Inside are two sensors, one is a classic 3-axis accelerometer, which can tell you which direction is down towards the Earth (by measuring gravity). The other is a magnetometer that can sense where the strongest magnetic force is coming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
