# Fritzing sketch lolin32 and mcp9808 (saved by Fritzing 0.9.3b)

parts:
  U1 = lolin
  Part2 = MCP9808 High Accuracy I2C Temperature Sensor [part_number=1782]

nets:
  N1: U1.connector32, Part2.SDA
  N2: U1.connector33, Part2.SCL
  N3: U1.connector34, Part2.VDD
  N4: U1.connector37, Part2.GND

custom parts:
  MCP9808 High Accuracy I2C Temperature Sensor: This I2C digital temperature sensor is one of the more accurate/precise we've ever seen, with a typical accuracy of ±0.25°C over the sensor's -40°C to +125°C range and precision of +0.0625°C. They work great with any microcontroller using standard i2c. There are 3 address pins so you can connect up to 8 to a single I2C bus without address collisions. Best of all, a wide voltage range makes is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
