# Fritzing sketch lolin32 and mma8451 (saved by Fritzing 0.9.3b)

parts:
  U1 = lolin
  Part1 = Adafruit MMA8451 Accelerometer [part_number="Adafruit #2019"]

nets:
  N1: U1.connector32, Part1.SDA
  N2: U1.connector33, Part1.SCL
  N3: U1.connector34, Part1.VIN
  N4: U1.connector37, Part1.GND

custom parts:
  Adafruit MMA8451 Accelerometer: So many accelerometers and so little time! We've expanded our accelerometer selection even more with this high-precision and inexpensive MMA8451 Triple-Axis Accelerometer w/ 14-bit ADC. You can detect motion, tilt and basic orientation with a digital accelerometer - and the MMA8451 is a great accelerometer to start with. It has a wide usage range, from +-2g up to +-8g yet is easy to use with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
