# Fritzing sketch lolin32 and sht31 (saved by Fritzing 0.9.3b)

parts:
  U1 = lolin
  Part4 = Adafruit SHT31-D Sensirion Temperature/Humidity Sensor [part_number="Adafruit #2857"]

nets:
  N1: U1.connector31, Part4.GND
  N2: U1.connector32, Part4.SDA
  N3: U1.connector33, Part4.SCL
  N4: U1.connector34, Part4.VIN

custom parts:
  Adafruit SHT31-D Sensirion Temperature/Humidity Sensor: Sensirion Temperature/Humidity sensors are some of the finest & highest-accuracy devices you can get. And, finally we have some that have a true I2C interface for easy reading. The SHT31-D sensor has an excellent ±2% relative humidity and ±0.3°C accuracy for most uses. Unlike earlier SHT sensors, this sensor has a true I2C interface, and (bonus!) even with two address options. It also is 3V or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
