# Fritzing sketch lolin32 andhdc1008 (saved by Fritzing 0.9.3b)

parts:
  Part1 = Adafruit HDC1008 Temperature Humidity Sensor [part_number="Adafruit #2635"]
  U1 = lolin

nets:
  N1: Part1.VDD, U1.connector34
  N2: Part1.GND, U1.connector37
  N3: Part1.SCL, U1.connector33
  N4: Part1.SDA, U1.connector32

custom parts:
  Adafruit HDC1008 Temperature Humidity Sensor: This I2C digital humidity sensor is a fairly accurate and intelligent alternative to the much simpler Humidity and Temperature Sensor - SHT15 Breakout It has a typical accuracy of ±4% with an operating range that's optimized from 10% to 80% RH. Operation outside this range is still possible - just the accuracy might drop a bit. The temperature output has a typical accuracy of ±0.2°C from -20~85°C.
